// Logisim project ex4_test.circ as structural Verilog: 1 circuit, main circuit main
module main (
  output [7:0] out_1,
  output Out1,
  output [7:0] Out2,
  output [7:0] out_4
);

  wire clock_1_out;
  wire [7:0] adder_1_out;

  Clock clock_1 (.out(clock_1_out));
  Adder adder_1 (.a(8'h1), .b(out_1), .out(adder_1_out));  // open: cin, cout
  Register register_1 (.D(adder_1_out), .clk(clock_1_out), .Q(out_1));  // open: en, clr
  ROM rom_1 (.addr(out_1), .data(out_4));
  Split split_1 (.In1(out_4), .Out1(Out1), .Out2(Out2));

  // Other names for the same wires on the sheet: In1[7:0] = out_4; Test[7:0] = out_1

  // Notes on the sheet:
  //   contents of rom_1 (hex, n*v repeats v):
  //   1 80 81
  //   Your Split circuit must fit here!
  //   There should be no red or blue wires, and the result should not be all X's
endmodule
